# Fritzing sketch circuito (saved by Fritzing 0.9.2b)
breadboards: 2

parts:
  Parte1 = Arduino Mega 2560 (Rev3)
  Parte2 = Arduino GSM Shield
  LCD1 = LCD screen
  R2 = Rotary Potentiometer (Small) [maximum_resistance=100kΩ package=THT]
  Parte3 = SRF05 Ultrasonic Rangefinder
  J1 = Piezo Speaker
  R3 = Resistor [tolerance=±5% resistance=220 package=THT]
  LED1 = LED - 5mm [color="Red (633nm)" package="5 mm [THT]"]
  Parte4 = RFID-RC522-v2

nets:
  N1: Parte1.D23, LCD1.DB7
  N2: Parte1.D25, LCD1.DB6
  N3: Parte1.D27, LCD1.DB5
  N4: Parte1.D29, LCD1.DB4
  N5: Parte1.D31, LCD1.RS
  N6: Parte1.D33, LCD1.R/W
  N7: Parte1.D35, J1.pin2
  N8: Parte1.D37, LED1.anode
  N9: Parte1.D39, Parte3.Trig
  N10: Parte1.D41, Parte3.Echo
  N11: Parte1.D49, Parte4.RST
  N12: Parte1.D50, Parte4.MISO
  N13: Parte1.D51, Parte4.MOSI
  N14: Parte1.D52, Parte4.SCK
  N15: Parte1.D53, Parte4.SDA
  GND: Parte1.GND, Parte4.GND
  3V3: Parte2.3V3, Parte4.3.3V
  5V: Parte2.5V, LCD1.VDD, LCD1.LED+, R2.leg2, Parte3.VCC
  VSS: Parte2.AGND, LCD1.VSS, LCD1.LED-, R2.leg1, Parte3.GND, J1.pin1, R3.Pin_0
  N16: LCD1.V0, LCD1.E, R2.wiper

custom parts:
  RFID-RC522-v2: A simple China made RFID-RC522 Reader; do check the pin labels, as this is a MFRC522 based clone.
